// Logisim project JKjoint-01.circ as structural Verilog: 1 circuit, main circuit main
module main (
  input  w,
  input  x,
  input  y,
  input  z,
  output out_5
);

  wire and_1_out, and_2_out, and_4_out, or_1_out;

  // NOT_Gate not_1 has open pins: in=w, out=open
  // NOT_Gate not_2 has open pins: in=x, out=open
  // NOT_Gate not_3 has open pins: in=y, out=open
  // NOT_Gate not_4 has open pins: in=z, out=open
  // AND_Gate and_1 has open pins: out=and_1_out
  // AND_Gate and_2 has open pins: out=and_2_out
  // AND_Gate and_3 is placed but not wired
  // AND_Gate and_4 has open pins: out=and_4_out
  // AND_Gate and_5 has open pins: in0=and_1_out, out=open
  // AND_Gate and_6 has open pins: in0=and_2_out, out=open
  // AND_Gate and_7 has open pins: in0=and_4_out, out=open
  // OR_Gate or_1 has open pins: out=or_1_out
  buf or_2 (out_5, or_1_out);  // OR_Gate
endmodule
